// Logisim project A1CPSC359.circ as structural Verilog: 3 circuits, main circuit main
module main (
);

  wire clock_1_out, controller_1_cg, controller_1_cr, controller_1_cy, controller_1_pg, controller_1_pr,
       counter_1_a, counter_1_w, counter_1_y, counter_1_z;

  Clock clock_1 (.out(clock_1_out));
  Counter counter_1 (.in_1(clock_1_out), .A(counter_1_a), .y(counter_1_y), .z(counter_1_z), .w(counter_1_w));
  Controller controller_1 (
    .x(counter_1_a), .y(counter_1_y), .z(counter_1_z), .w(counter_1_w), .CR(controller_1_cr),
    .CY(controller_1_cy), .CG(controller_1_cg), .PR(controller_1_pr), .PG(controller_1_pg));
  LED CR (.in(controller_1_cr));
  LED CY (.in(controller_1_cy));
  LED CG (.in(controller_1_cg));
  LED PR (.in(controller_1_pr));
  LED PG (.in(controller_1_pg));
endmodule

module Counter (
  input  in_1,
  output A,
  output y,
  output z,
  output w
);

  wire and_1_out, and_2_out, JA_out, JB_out, KA_out, KB_out, not_1_out, not_2_out, not_3_out, not_4_out,
       or_1_out;

  or or_1 (or_1_out, and_1_out, and_2_out);
  and and_1 (and_1_out, not_4_out, not_1_out);
  and and_2 (and_2_out, not_4_out, not_2_out);
  and KB (KB_out, w, z, y, not_1_out);
  and JB (JB_out, w, z, not_2_out, not_1_out);
  and KA (KA_out, w, z, not_2_out, A);
  and JA (JA_out, w, z, y, not_1_out);
  not not_1 (not_1_out, A);
  J_K_Flip_Flop x (.J(JA_out), .clk(in_1), .K(KA_out), .Q(A));  // open: Qn, preset, en, reset
  not not_2 (not_2_out, y);
  J_K_Flip_Flop u_y (.J(JB_out), .clk(in_1), .K(KB_out), .Q(y));  // open: Qn, preset, en, reset
  J_K_Flip_Flop u_z (.J(w), .clk(in_1), .K(w), .Q(z));  // open: Qn, preset, en, reset
  not not_3 (not_3_out, z);
  not not_4 (not_4_out, w);
  J_K_Flip_Flop u_w (.J(or_1_out), .clk(in_1), .K(1'b1), .Q(w));  // open: Qn, preset, en, reset
endmodule

module Controller (
  input  x,
  input  y,
  input  z,
  input  w,
  output CR,
  output CY,
  output CG,
  output PR,
  output PG
);

  wire and_3_out, and_4_out, and_5_out, and_6_out, and_7_out, not_1_out, not_2_out, not_3_out, not_4_out;

  not not_1 (not_1_out, x);
  not not_2 (not_2_out, y);
  not not_3 (not_3_out, z);
  not not_4 (not_4_out, w);
  and and_1 (CR, x, not_2_out);
  and and_2 (CY, not_1_out, y, z);
  and and_3 (and_3_out, not_1_out, not_2_out);
  and and_4 (and_4_out, not_1_out, not_3_out);
  and and_5 (and_5_out, not_2_out, z, w);
  and and_6 (and_6_out, x, not_2_out, not_3_out);
  and and_7 (and_7_out, x, not_2_out, not_4_out);
  LED u_CR (.in(CR));
  LED u_CY ();  // open: in
  LED u_CG (.in(CG));
  or or_1 (CG, and_3_out, and_4_out);
  LED u_PR (.in(PR));
  or or_2 (PR, not_1_out, and_5_out);
  LED u_PG (.in(PG));
  or or_3 (PG, and_6_out, and_7_out);
endmodule
